# Fritzing sketch HardwareSetup_ProMicro_RX (saved by Fritzing 0.9.3b)

parts:
  Antenna2 = HC-12 Antenna
  HC-2 = HC-12 Module
  Q1 = MOSFET-NCHANNEL [package=to220v]
  U1 = Vibration Motor- ROB-08449 [package=vibe-motor-10mm]
  Pro_Micro1 = Pro Micro
  OLED_I2C1 = OLED 128x64 I2C Monochrome Display
  RE1 = Rotary Encoder [package=THT]
  Part6 = NCP1400 Step-Up Breakout
  U4 = LIPO-1000mAh [package=lipo-1000]
  S3 = Toggle Switch [package=THT]
  D2 = Rectifier Diode [package="Melf DO-213 AA [SMD]"]
  R2 = Resistor [tolerance=±5% resistance=47k package=THT]
  R1 = Resistor [tolerance=±5% resistance=47k package=THT]
  R3 = Resistor [tolerance=±5% resistance=10k package="1206 [SMD]"]

nets:
  N1: Antenna2.ANT, HC-2.ANT
  N2: HC-2.TXD, Pro_Micro1.RX0
  GND: HC-2.GND, Pro_Micro1.GND, OLED_I2C1.GND, RE1.EncoderPinC
  N3: HC-2.VCC, D2.cathode
  N4: Q1.G, Pro_Micro1.D10, R3.Pin_1
  N5: Q1.D, U1.+
  N6: Q1.S, Part6.GND, U4.-, R3.Pin_0
  VCC: U1.-, Pro_Micro1.VCC, OLED_I2C1.VDD, Part6.VOUT
  N7: Pro_Micro1.D2, OLED_I2C1.SDA
  N8: Pro_Micro1.D3, OLED_I2C1.SCK
  N9: Pro_Micro1.D7, RE1.EncoderPinA, R1.Pin_0
  N10: Pro_Micro1.D8, RE1.EncoderPinB, R2.Pin_0
  N11: Part6.VIN, S3.COM
  N12: U4.+, S3.L1

custom parts:
  HC-12 Antenna: Antenna for HC-12 433Mhz Module
  HC-12 Module: HC-12 433Mhz Module
  Pro Micro: The SparkFun Pro Micro is a complete USB-based microcontoller development system, in a very small footprint, capable of implementing many types of projects. All programming can be done via the USB port.
