# Fritzing sketch HardwareSetup_ProMicro_TX (saved by Fritzing 0.9.3b)

parts:
  Antenna2 = HC-12 Antenna
  HC-2 = HC-12 Module
  Part4 = LIDAR-Lite
  C2 = Electrolytic Capacitor [capacitance=1µF package="100 mil [THT, electrolytic]"]
  Pro_Micro3 = Pro Micro
  Part5 = NCP1400 Step-Up Breakout
  U3 = LIPO-1000mAh [package=lipo-1000]
  S2 = Toggle Switch [package=THT]
  Part6 = 10-DOF IMU L3GD20H + LSM303 + BMP180 [part_number=1604]
  D1 = Rectifier Diode [package="Melf DO-213 AA [SMD]"]

nets:
  N1: Antenna2.ANT, HC-2.ANT
  N2: HC-2.RXD, Pro_Micro3.TX1
  GND: HC-2.GND, Part4.GND, C2.-, Pro_Micro3.GND, Part5.GND, U3.-, Part6.GND
  N3: HC-2.VCC, D1.cathode
  N4: Part4.5V, C2.+, D1.anode
  N5: Part4.SCL, Pro_Micro3.D3, Part6.SCL
  N6: Part4.SDA, Pro_Micro3.D2, Part6.SDA
  N7: Part5.VOUT, Part6.VIN
  N8: Part5.VIN, S2.COM
  N9: U3.+, S2.L1

custom parts:
  HC-12 Antenna: Antenna for HC-12 433Mhz Module
  HC-12 Module: HC-12 433Mhz Module
  LIDAR-Lite: PulsedLight LIDAR-Lite Sensor
  Pro Micro: The SparkFun Pro Micro is a complete USB-based microcontoller development system, in a very small footprint, capable of implementing many types of projects. All programming can be done via the USB port.
  10-DOF IMU L3GD20H + LSM303 + BMP180: This inertial-measurement-unit combines 3 of the best quality sensors available on the market to give you 11 axes of data: 3 axes of accelerometer data, 3 axes gyroscopic, 3 axes magnetic (compass), barometric pressure/altitude and temperature. We tested many different 'combination' sensors and found these were the best value, with stable and reliable readings.
